# Fritzing sketch ESP8266-Arduino-Node-Custom (saved by Fritzing 0.9.3b)

parts:
  WeMos_D1_Mini1 = WeMos D1 Mini
  Part1 = Adafruit Pixie [part_number="Adafruit #2741"]
  U2 = HALL-EFFECT [package=sc70]
  Part2 = Adafruit Pixie [part_number="Adafruit #2741"]
  Part3 = Adafruit Pixie [part_number="Adafruit #2741"]
  Part4 = Adafruit Pixie [part_number="Adafruit #2741"]

nets:
  5V: WeMos_D1_Mini1.5V, Part1.5V, U2.VCC, Part2.5V, Part3.5V, Part4.5V
  N1: WeMos_D1_Mini1.D1, Part2.IN
  N2: WeMos_D1_Mini1.D2, U2.OUT
  N3: WeMos_D1_Mini1.D3, Part1.IN
  N4: WeMos_D1_Mini1.D4, Part3.IN
  N5: WeMos_D1_Mini1.D5, Part4.IN
  GND: WeMos_D1_Mini1.G, Part1.GND, U2.GND, Part2.GND, Part3.GND, Part4.GND

notes:
  Hall Sensor
  PWM Power LEDs

custom parts:
  Adafruit Pixie: NeoPixels are plenty bright, suuuure. BUT ARE THEY 3 WATTS BRIGHT? No! They are not! That's why you need a Pixie. These chainable smart LEDs are not only super-smart, they are ridonkulously bright with 3W total, compared to 0.2W of a 'standard' NeoPixel. Designed by Ytai Ben-Tsvi, these are the ultimate in LEDs.
