# Fritzing sketch ESP8266-Arduino-Node (saved by Fritzing 0.9.3b)

parts:
  WeMos_D1_Mini1 = WeMos D1 Mini
  NEOPIXEL1 = Neopixel Strip -- Black (60/m)
  Part1 = Adafruit Pixie [part_number="Adafruit #2741"]
  U2 = HALL-EFFECT [package=sc70]

nets:
  5V: WeMos_D1_Mini1.5V, NEOPIXEL1.+5V, Part1.5V, U2.VCC
  N1: WeMos_D1_Mini1.D1, U2.OUT
  N2: WeMos_D1_Mini1.D2, NEOPIXEL1.DI
  N3: WeMos_D1_Mini1.D3, Part1.IN
  GND: WeMos_D1_Mini1.G, NEOPIXEL1.GND, Part1.GND, U2.GND

notes:
  Hall Sensor
  PWM Power LED
  Addressable LED

custom parts:
  Neopixel Strip -- Black (60/m): Neopixel Strip, Black, 60 pixels per meter.
  Adafruit Pixie: NeoPixels are plenty bright, suuuure. BUT ARE THEY 3 WATTS BRIGHT? No! They are not! That's why you need a Pixie. These chainable smart LEDs are not only super-smart, they are ridonkulously bright with 3W total, compared to 0.2W of a 'standard' NeoPixel. Designed by Ytai Ben-Tsvi, these are the ultimate in LEDs.
